# Fritzing sketch Arduino LED (saved by Fritzing 0.9.3b)
breadboards: 1

parts:
  Arduino = Arduino Uno (Rev3)
  R1 = Resistor [tolerance=±5% resistance=220 package=THT]
  LED1 = LED - 5mm [color="Red (633nm)" package="5 mm [THT]"]

nets:
  N1: Arduino.D13/SCK, LED1.anode
  N2: Arduino.GND, R1.Pin_1
  N3: R1.Pin_0, LED1.cathode

notes:
  Arduino LED Circuit
