# Fritzing sketch Traffic Light (saved by Fritzing 0.9.3b)
breadboards: 1

parts:
  Part1 = Arduino Uno (Rev3)
  R1 = Resistor [tolerance=±5% resistance=220 package=THT]
  LED1 = LED - 5mm [color="Red (633nm)" package="5 mm [THT]"]
  R2 = Resistor [tolerance=±5% resistance=220 package=THT]
  R3 = Resistor [tolerance=±5% resistance=220 package=THT]
  LED3 = LED - 5mm [color="Green (560nm)" package="5 mm [THT]"]
  LED2 = LED - 5mm [color="Yellow (585nm)" package="5 mm [THT]"]

nets:
  N1: Part1.D11_PWM/MOSI, R3.Pin_0
  N2: Part1.D12/MISO, R2.Pin_0
  N3: Part1.D13/SCK, R1.Pin_0
  N4: Part1.GND, LED1.cathode, LED3.cathode, LED2.cathode
  N5: R1.Pin_1, LED1.anode
  N6: R2.Pin_1, LED2.anode
  N7: R3.Pin_1, LED3.anode
