# Fritzing sketch Cart (saved by Fritzing 0.9.3b)
breadboards: 1

parts:
  IC2 = L293D [package=THT]
  Part1 = Arduino Uno (Rev3)
  M2 = DC Motor
  M1 = DC Motor

nets:
  N1: IC2.Enable_1, Part1.D10_PWM/SS
  N2: IC2.In_1, Part1.D8
  N3: IC2.Out_1_(_Controlled_by_Enable_1_), M1.pin_2
  N4: IC2.0V, Part1.GND
  N5: IC2.Out_2_(_Controlled_by_Enable_1_), M1.pin_1
  N6: IC2.In_2, Part1.D7
  N7: IC2.+Vmotor, IC2.+V, Part1.5V
  N8: IC2.Enable_2, Part1.D9_PWM
  N9: IC2.In_3, Part1.D6_PWM
  N10: IC2.Out_3_(_Controlled_by_Enable_2_), M2.pin_2
  N11: IC2.Out_4_(_Controlled_by_Enable_2_), M2.pin_1
  N12: IC2.In_4, Part1.D5_PWM
